# Fritzing sketch Final Project (saved by Fritzing 0.9.3b)
breadboards: 2

parts:
  A1 = DHT22 module
  OLED_I2C1 = OLED 128x64 I2C Monochrome Display
  M1 = BME280
  U1 = ESP32-38PinWide [part_number=ESP32-38PinWide]
  Capacitive_Soil_Moisture_Sensor1 = DFRobot Capacitive Soil Moisture Sensor V1.0 [part_number=SEN0193]

nets:
  GND: A1.GND, OLED_I2C1.GND, M1.GND, U1.GND, Capacitive_Soil_Moisture_Sensor1.GND
  VCC: A1.VCC, OLED_I2C1.VDD, U1.3.3, Capacitive_Soil_Moisture_Sensor1.VCC
  N1: A1.DAT, U1.GPIO19
  N2: OLED_I2C1.SDA, M1.SDA, U1.GPIO21
  N3: OLED_I2C1.SCK, M1.SCL, U1.GPIO22
  VIN: M1.VIN, U1.VIN
  N4: U1.GPIO34, Capacitive_Soil_Moisture_Sensor1.A

custom parts:
  DHT22 module: DHT22 module. Pins GND VCC Data.
  BME280: Temperature Humidity Barometric presure Sensor
  ESP32-38PinWide: Generic 38-Pin ESP32 with wide format (only access to one side of pins on a breadboard) based on Stephen Lilley's HiLetgo ESP-WROOM-32 ESP32 ESP-32S Development Board.
  DFRobot Capacitive Soil Moisture Sensor V1.0: DFRobot Capacitive Soil Moisture Sensor V1.0 This product measures soil moisture levels by capacitive sensing, rather than resistive sensing like other types of moisture sensor. It is made of a corrosion resistant material giving it a long service life. Insert it into soil and impress your friends with the real-time soil moisture data! The product includes an on-board voltage regulator which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
